// Digital circuit MUX.dig as structural Verilog
module MUX (
  input  D,
  input  C,
  input  B,
  input  A,
  output Y
);

  wire not_1_out;

  not not_1 (not_1_out, C);
  Multiplexer #(.Selector_Bits(3)) multiplexer_1 (
    .sel({3{C}}), .in_0(1'b0), .in_1(C), .in_2(C), .in_3(C), .in_4(not_1_out), .in_5(not_1_out),
    .in_6(not_1_out), .in_7(C), .out(Y));
  // also tied to VCC on the sheet: C

  // Notes on the sheet:
  //   Use A as the most-significant bit and 
  //   D as the least-significant bit.
  //   Converts between single bits & a 3-bit bus
endmodule

/* Test case:
A B C D Y
0 0 0 0 X
0 0 0 1 1
*/
